// Logisim project lab3_Kusmierz_Uziemblo.circ as structural Verilog: 6 circuits, main circuit zadanie1
module zadanie1 (
  input  a,
  input  b,
  input  c,
  input  d,
  output M
);

  wire and_1_out, and_2_out, and_3_out, and_4_out, not_1_out, not_2_out, not_3_out, not_4_out;

  not not_1 (not_1_out, a);
  not not_2 (not_2_out, b);
  not not_3 (not_3_out, c);
  not not_4 (not_4_out, d);
  and and_1 (and_1_out, not_1_out, not_3_out, d);
  and and_2 (and_2_out, not_2_out, not_3_out, not_4_out);
  and and_3 (and_3_out, a, b, not_4_out);
  and and_4 (and_4_out, b, c, d);
  or or_1 (M, and_1_out, and_2_out, and_3_out, and_4_out);

  // Notes on the sheet:
  //   M(a, b, c, d) = ((b' c) + (a' b d')) xor ((d ((a' + c)'))')
endmodule

module input_check (
  input  [2:0] X,
  input  [2:0] Y,
  input  [2:0] Z,
  output T
);

  wire and_1_out, and_2_out, and_3_out, bits_check_1_r, bits_check_2_r, bits_check_3_r;

  bits_check bits_check_1 (.A(X), .R(bits_check_1_r));
  bits_check bits_check_2 (.A(Y), .R(bits_check_2_r));
  bits_check bits_check_3 (.A(Z), .R(bits_check_3_r));
  and and_1 (and_1_out, bits_check_2_r, bits_check_3_r);
  and and_2 (and_2_out, bits_check_1_r, bits_check_3_r);
  and and_3 (and_3_out, bits_check_1_r, bits_check_2_r);
  or or_1 (T, and_1_out, and_2_out, and_3_out);
endmodule

module bits_check (
  input  [2:0] A,
  output R
);

  wire and_1_out, and_2_out, and_3_out, not_1_out, not_2_out, not_3_out;

  not not_1 (not_1_out, A[2]);
  not not_2 (not_2_out, A[1]);
  not not_3 (not_3_out, A[0]);
  and and_1 (and_1_out, not_1_out, not_2_out, A[0]);
  and and_2 (and_2_out, A[2], not_2_out, not_3_out);
  and and_3 (and_3_out, A[2], A[1], A[0]);
  or or_1 (R, and_1_out, and_2_out, and_3_out);
endmodule

module grid4x4 (
  input  CLR,
  input  [3:0] T
);

  wire k0_out, k1_out, k2_out, k3_out, w0_out, w1_out, w2_out, w3_out;

  and k0 (k0_out, ~T[3], ~T[2], ~CLR);  // AND_Gate
  and k1 (k1_out, ~T[3], T[2], ~CLR);  // AND_Gate
  and k2 (k2_out, T[3], ~T[2], ~CLR);  // AND_Gate
  and k3 (k3_out, T[3], T[2], ~CLR);  // AND_Gate
  and w0 (w0_out, ~T[1], ~T[0], ~CLR);  // AND_Gate
  and w1 (w1_out, ~T[1], T[0], ~CLR);  // AND_Gate
  and w2 (w2_out, T[1], ~T[0], ~CLR);  // AND_Gate
  and w3 (w3_out, T[1], T[0], ~CLR);  // AND_Gate
  // RGBLED D0: pin names not known; wires that end beside it: T[3], T[2], CLR, T[3], CLR, T[2], CLR, CLR, T[1], T[0], CLR
  // RGBLED D1: pin names not known; wires that end beside it: T[1], CLR
  // RGBLED D2: pin names not known; wires that end beside it: T[0], CLR
  // RGBLED D3: pin names not known; wires that end beside it: CLR, k0_out
  // RGBLED D4: pin names not known
  // RGBLED D5: pin names not known
  // RGBLED D6: pin names not known
  // RGBLED D7: pin names not known; wires that end beside it: k1_out
  // RGBLED D8: pin names not known
  // RGBLED D9: pin names not known
  // RGBLED DA: pin names not known
  // RGBLED DB: pin names not known; wires that end beside it: k2_out
  // RGBLED DC: pin names not known; wires that end beside it: w0_out
  // RGBLED DD: pin names not known; wires that end beside it: w1_out
  // RGBLED DE: pin names not known; wires that end beside it: w2_out
  // RGBLED DF: pin names not known; wires that end beside it: k3_out, w3_out
endmodule

module display (
  input  [1:0] A
);

  wire not_1_out, nP, P, Q, R;
  wire [0:0] ROW2;
  wire [3:2] ROW5;

  not not_1 (not_1_out, A[0]);
  and and_1 (P, A[1], not_1_out);
  not not_2 (nP, P);
  and and_2 (Q, A[1], A[0]);
  nor nor_1 (R, A[1], A[0]);
  or or_1 (ROW2[0], A[1], A[0]);
  xor xor_1 (ROW5[2], A[1], A[0]);
  not not_3 (ROW5[3], ROW5[2]);
  DotMatrix #(.inputtype("row"), .matrixcols(4), .matrixrows(5)) dotmatrix_1 (
    .row0({nP, {2{P}}, nP}), .row1({1'b1, Q, R, ROW2[0]}), .row2({1'b1, R, Q, ROW2[0]}),
    .row3({2'b10, R, ROW2[0]}), .row4({ROW5, ROW5[2], ROW5[3]}));

  // Other names for the same wires on the sheet: ROW1[3:0] = {nP, {2{P}}, nP}; ROW2[2:1] = {Q, R};
  //   ROW3[2:0] = {R, Q, ROW2[0]}; ROW4[1:0] = {R, ROW2[0]}; S = ROW2[0]; ROW5[1:0] = {ROW5[2], ROW5[3]};
  //   XO = ROW5[2]; XN = ROW5[3]

  // Notes on the sheet:
  //   WEJŚCIE
  //   A0
  //   A1
  //   BRAMKI - sygnały pomocnicze
  //   display: wejście A (2 bity) -> litera na matrycy LED 4x5   00=K   01=U   10=O   11=N
  //   wiersz 1
  //   wiersz 2
  //   wiersz 3
  //   wiersz 4
  //   wiersz 5
  //   5 splitterów 4-bitowych = 5 wierszy matrycy (ROW1..ROW5)
  //   tunele w wierszu od góry: kolumna 4, 3, 2, 1
  //   MATRYCA LED 4x5 (Rows)
endmodule

module zadanie5 (
  input  a,
  input  b,
  input  c,
  input  a2,
  input  b2,
  input  c2,
  output f,
  output f2
);

  wire and_1_out, and_2_out, and_3_out, and_4_out, and_5_out, and_6_out, and_8_out, not_1_out, not_2_out,
       not_3_out, not_4_out, not_5_out, not_6_out, or_1_out, or_2_out, or_3_out, or_4_out, or_5_out;

  and and_1 (and_1_out, a, b);
  not not_1 (not_1_out, c);
  and and_2 (and_2_out, a, b);
  or or_1 (or_1_out, a, b);
  not not_2 (not_2_out, c);
  not not_3 (not_3_out, a);
  not not_4 (not_4_out, b);
  not not_5 (not_5_out, c2);
  and and_3 (and_3_out, and_1_out, not_1_out);
  and and_4 (and_4_out, and_2_out, c);
  and and_5 (and_5_out, b, not_2_out);
  or or_2 (or_2_out, not_3_out, not_4_out);
  not not_6 (not_6_out, or_2_out);
  or or_3 (or_3_out, a2, not_5_out);
  and and_6 (and_6_out, or_1_out, and_5_out);
  and and_7 (f2, or_3_out, b2);
  and and_8 (and_8_out, not_6_out, c);
  or or_4 (or_4_out, and_3_out, and_4_out);
  or or_5 (or_5_out, or_4_out, and_6_out);
  or or_6 (f, or_5_out, and_8_out);

  // Notes on the sheet:
  //   T1 = abc'
  //   T2 = abc
  //   T3 = (a+b)(bc')
  //   T4 = ((a'+b')')c
  //   f(a,b,c) przed uproszczeniem: abc' + abc + (a+b)(bc') + ((a'+b')')c
  //   f2(a2,b2,c2) po uproszczeniu: b(a + c') = ab + bc'
  //   f = T1 + T2 + T3 + T4
endmodule
